// Logisim project CPU.circ as structural Verilog
module main (
);

  wire cpu_1_out_3, cpu_1_out_4, cpu_1_out_5, cpu_1_out_6, cpu_1_out_7, cpu_1_out_8, cpu_1_out_9,
       cpu_1_out_10, Hard_Drive_out_1, Hard_Drive_out_2, Hard_Drive_out_3, Hard_Drive_out_4,
       Hard_Drive_out_5, Hard_Drive_out_6, Hard_Drive_out_7, Hard_Drive_out_8, Hard_Drive_out_9,
       Hard_Drive_out_10, Hard_Drive_out_11, Hard_Drive_out_12, undriven, undriven_2;

  External_Device Hard_Drive (
    .out_1(Hard_Drive_out_1), .out_2(Hard_Drive_out_2), .out_3(Hard_Drive_out_3), .out_4(Hard_Drive_out_4),
    .out_5(Hard_Drive_out_5), .out_6(Hard_Drive_out_6), .out_7(Hard_Drive_out_7), .out_8(Hard_Drive_out_8),
    .out_9(Hard_Drive_out_9), .out_10(Hard_Drive_out_10), .out_11(Hard_Drive_out_11),
    .out_12(Hard_Drive_out_12));
  External_Device Monitor (
    .out_1(Hard_Drive_out_4), .out_2(Hard_Drive_out_3), .out_3(Hard_Drive_out_2), .out_4(Hard_Drive_out_1),
    .out_5(Hard_Drive_out_5), .out_6(Hard_Drive_out_6), .out_7(Hard_Drive_out_7), .out_8(Hard_Drive_out_8),
    .out_9(Hard_Drive_out_9), .out_10(Hard_Drive_out_10), .out_11(Hard_Drive_out_11),
    .out_12(Hard_Drive_out_12));
  External_Device Keyboard (
    .out_1(Hard_Drive_out_4), .out_2(Hard_Drive_out_3), .out_3(Hard_Drive_out_2), .out_4(Hard_Drive_out_1),
    .out_5(Hard_Drive_out_5), .out_6(Hard_Drive_out_6), .out_7(Hard_Drive_out_7), .out_8(Hard_Drive_out_8),
    .out_9(Hard_Drive_out_9), .out_10(Hard_Drive_out_10), .out_11(Hard_Drive_out_11),
    .out_12(Hard_Drive_out_12));
  CPU cpu_1 (
    .out_3(cpu_1_out_3), .out_4(cpu_1_out_4), .out_5(cpu_1_out_5), .out_6(cpu_1_out_6), .out_7(cpu_1_out_7),
    .out_8(cpu_1_out_8), .out_9(cpu_1_out_9), .out_10(cpu_1_out_10), .out_15(Hard_Drive_out_12),
    .out_16(Hard_Drive_out_11), .out_17(Hard_Drive_out_10), .out_18(Hard_Drive_out_9),
    .out_19(Hard_Drive_out_8), .out_20(Hard_Drive_out_7), .out_21(Hard_Drive_out_6),
    .out_22(Hard_Drive_out_5), .out_11(Hard_Drive_out_4), .out_12(Hard_Drive_out_3),
    .out_13(Hard_Drive_out_2), .out_14(Hard_Drive_out_1), .in_1(undriven), .in_2(undriven_2));
  RAM RAM (
    .out_3(cpu_1_out_3), .out_4(cpu_1_out_4), .out_5(cpu_1_out_5), .out_6(cpu_1_out_6), .out_7(cpu_1_out_7),
    .out_8(cpu_1_out_8), .out_9(cpu_1_out_9), .out_10(cpu_1_out_10), .out_11(Hard_Drive_out_5),
    .out_12(Hard_Drive_out_6), .out_13(Hard_Drive_out_7), .out_14(Hard_Drive_out_8),
    .out_15(Hard_Drive_out_9), .out_16(Hard_Drive_out_10), .out_17(Hard_Drive_out_11),
    .out_18(Hard_Drive_out_12), .in_1(undriven), .in_2(undriven_2));

  // Notes on the sheet:
  //   Control Bus
  //   Address Bus
  //   Data Bus
  //   Set
  //   Enable
endmodule

module CPU (
  input  in_1,
  input  in_2,
  output out_3,
  output out_4,
  output out_5,
  output out_6,
  output out_7,
  output out_8,
  output out_9,
  output out_10,
  output out_11,
  output out_12,
  output out_13,
  output out_14,
  output out_15,
  output out_16,
  output out_17,
  output out_18,
  output out_19,
  output out_20,
  output out_21,
  output out_22
);
endmodule

module External_Device (
  output out_1,
  output out_2,
  output out_3,
  output out_4,
  output out_5,
  output out_6,
  output out_7,
  output out_8,
  output out_9,
  output out_10,
  output out_11,
  output out_12
);
endmodule

module RAM (
  input  in_1,
  input  in_2,
  output out_3,
  output out_4,
  output out_5,
  output out_6,
  output out_7,
  output out_8,
  output out_9,
  output out_10,
  output out_11,
  output out_12,
  output out_13,
  output out_14,
  output out_15,
  output out_16,
  output out_17,
  output out_18
);
endmodule

module CPU_RAM (
);

  wire cpu_1_out_15, cpu_1_out_16, cpu_1_out_17, cpu_1_out_18, cpu_1_out_19, cpu_1_out_20, cpu_1_out_21,
       cpu_1_out_22, RAM_out_3, RAM_out_4, RAM_out_5, RAM_out_6, RAM_out_7, RAM_out_8, RAM_out_9, RAM_out_10;

  CPU cpu_1 (
    .out_15(cpu_1_out_15), .out_16(cpu_1_out_16), .out_17(cpu_1_out_17), .out_18(cpu_1_out_18),
    .out_19(cpu_1_out_19), .out_20(cpu_1_out_20), .out_21(cpu_1_out_21), .out_22(cpu_1_out_22));  // open: out_3, out_4, out_5, out_6, out_7, out_8, out_9, out_10, out_11, out_12, out_13, out_14, in_1, in_2
  RAM RAM (
    .out_3(RAM_out_3), .out_4(RAM_out_4), .out_5(RAM_out_5), .out_6(RAM_out_6), .out_7(RAM_out_7),
    .out_8(RAM_out_8), .out_9(RAM_out_9), .out_10(RAM_out_10), .out_11(cpu_1_out_22), .out_12(cpu_1_out_21),
    .out_13(cpu_1_out_20), .out_14(cpu_1_out_19), .out_15(cpu_1_out_18), .out_16(cpu_1_out_17),
    .out_17(cpu_1_out_16), .out_18(cpu_1_out_15), .in_1(1'b0), .in_2(1'b1));
  // also tied to GND on the sheet: {RAM_out_3, RAM_out_4, RAM_out_6, RAM_out_7, RAM_out_8}
  // also tied to VCC on the sheet: {RAM_out_5, RAM_out_9, RAM_out_10}

  // Notes on the sheet:
  //   -------->
  //   ---------->
  //   <----------
  //   Address Bus
  //   Set
  //   Enable
  //   Data Bus
endmodule

module CPU_detailed (
  input  [7:0] in_1,
  input  [7:0] in_2,
  input  [7:0] in_3,
  input  [7:0] in_4,
  input  [7:0] in_5,
  input  [7:0] in_6,
  input  [7:0] in_7,
  output [7:0] out_8,
  output [7:0] out_9
);

  ALU alu_1 ();
  Control_Unit control_unit_1 ();
  RAM ram_1 (
    .out_3(in_1[0]), .out_4(in_1[1]), .out_5(in_1[2]), .out_6(in_1[3]), .out_7(in_1[4]), .out_8(in_1[7]),
    .out_9(in_1[7]), .out_10(in_1[7]), .out_11(in_1[7]), .out_12(in_1[7]), .out_13(in_1[7]),
    .out_14(in_1[4]), .out_15(in_1[3]), .out_16(in_1[2]), .out_17(in_1[1]), .out_18(in_1[0]));  // open: in_1, in_2

  assign in_1[6:5] = {2{in_1[7]}};
  assign in_2 = {{3{in_1[7]}}, in_1[4:0]};
  assign in_3 = {{3{in_1[7]}}, in_1[4:0]};
  assign in_4 = {{3{in_1[7]}}, in_1[4:0]};
  assign in_5 = {in_1[0], in_1[1], in_1[2], in_1[3], in_1[4], {3{in_1[7]}}};
  assign in_6 = {in_1[0], in_1[1], in_1[2], in_1[3], in_1[4], {3{in_1[7]}}};
  assign in_7 = {in_1[0], in_1[1], in_1[2], in_1[3], in_1[4], {3{in_1[7]}}};
  assign out_8 = {{3{in_1[7]}}, in_1[4:0]};
  assign out_9 = {{3{in_1[7]}}, in_1[4:0]};
endmodule
